// Logisim project 32BIT_CPU.circ as structural Verilog: 9 circuits, main circuit 32-Bit_DATA-PATH
module main (
  input  in_1,
  input  in_2,
  input  in_3,
  input  CLK,
  input  in_5,
  input  in_6
);

  wire [1:0] adder_1_out, bit_extender_1_out, register_1_q;
  wire [15:0] n16bit_alu_1_out_5, reg_file_1_rd1, reg_file_1_rd2, rom_1_data;

  Register #(.width(2)) register_1 (.D(adder_1_out), .en(in_2), .Q(register_1_q), .clk(in_1), .clr(in_3));
  ROM #(.addrWidth(2), .dataWidth(16)) rom_1 (.addr(register_1_q), .data(rom_1_data));  // open: sel
  Adder #(.width(2)) adder_1 (.a(2'b01), .b(register_1_q), .out(adder_1_out));  // open: cin, cout
  REG_FIle reg_file_1 (
    .WriteData(n16bit_alu_1_out_5), .Write_Reg(rom_1_data[3:0]), .RegWrite(in_5), .CLK(CLK),
    .RD1(reg_file_1_rd1), .RS(rom_1_data[11:8]), .RD2(reg_file_1_rd2), .RT(rom_1_data[7:4]));
  _16BIT_ALU u_16bit_alu_1 (
    .in_3(reg_file_1_rd1), .in_4(reg_file_1_rd2), .out_5(n16bit_alu_1_out_5), .in_1(in_6),
    .in_2(bit_extender_1_out));  // open: Cout
  Bit_Extender #(.in_width(4), .out_width(2)) bit_extender_1 (.in(rom_1_data[15:12]), .out(bit_extender_1_out));

  // Notes on the sheet:
  //   contents of rom_1 (hex, n*v repeats v):
  //   2426 2981
endmodule

module ALU (
  input  B,
  input  A,
  input  Cin,
  input  [1:0] in_4,
  output out_5,
  output out_6
);

  wire adder_1_out, and_1_out, and_2_out, multiplexer_1_out, not_1_out, or_1_out;

  not not_1 (not_1_out, B);
  Multiplexer #(.enable("false")) multiplexer_1 (.in0(B), .in1(not_1_out), .out(multiplexer_1_out), .sel(and_2_out));
  and and_1 (and_1_out, A, B);
  or or_1 (or_1_out, A, B);
  Adder #(.width(1)) adder_1 (.a(A), .b(multiplexer_1_out), .out(adder_1_out), .cin(Cin), .cout(out_6));
  and and_2 (and_2_out, in_4[0], in_4[1]);
  Multiplexer #(.select(2), .enable("false")) multiplexer_2 (
    .in0(and_1_out), .in1(or_1_out), .in2(adder_1_out), .in3(adder_1_out), .out(out_5), .sel(in_4));
endmodule

module _16BIT_ALU (
  input  in_1,
  input  [1:0] in_2,
  input  [15:0] in_3,
  input  [15:0] in_4,
  output [15:0] out_5,
  output Cout
);

  wire alu_1_out_6, alu_2_out_6, alu_3_out_6, alu_4_out_6, alu_5_out_6, alu_6_out_6, alu_7_out_6,
       alu_8_out_6, alu_9_out_6, alu_10_out_6, alu_11_out_6, alu_12_out_6, alu_13_out_6, alu_14_out_6,
       alu_15_out_6;

  ALU alu_1 (.out_5(out_5[0]), .B(in_4[0]), .A(in_3[0]), .Cin(in_1), .out_6(alu_1_out_6), .in_4(in_2));
  ALU alu_2 (.out_5(out_5[1]), .B(in_4[1]), .A(in_3[1]), .Cin(alu_1_out_6), .out_6(alu_2_out_6), .in_4(in_2));
  ALU alu_3 (.out_5(out_5[2]), .B(in_4[2]), .A(in_3[2]), .Cin(alu_2_out_6), .out_6(alu_3_out_6), .in_4(in_2));
  ALU alu_4 (.out_5(out_5[3]), .B(in_4[3]), .A(in_3[3]), .Cin(alu_3_out_6), .out_6(alu_4_out_6), .in_4(in_2));
  ALU alu_5 (.out_5(out_5[4]), .B(in_4[4]), .A(in_3[4]), .Cin(alu_4_out_6), .out_6(alu_5_out_6), .in_4(in_2));
  ALU alu_6 (.out_5(out_5[5]), .B(in_4[5]), .A(in_3[5]), .Cin(alu_5_out_6), .out_6(alu_6_out_6), .in_4(in_2));
  ALU alu_7 (.out_5(out_5[6]), .B(in_4[6]), .A(in_3[6]), .Cin(alu_6_out_6), .out_6(alu_7_out_6), .in_4(in_2));
  ALU alu_8 (.out_5(out_5[7]), .B(in_4[7]), .A(in_3[7]), .Cin(alu_7_out_6), .out_6(alu_8_out_6), .in_4(in_2));
  ALU alu_9 (.out_5(out_5[8]), .B(in_4[8]), .A(in_3[8]), .Cin(alu_8_out_6), .out_6(alu_9_out_6), .in_4(in_2));
  ALU alu_10 (.out_5(out_5[9]), .B(in_4[9]), .A(in_3[9]), .Cin(alu_9_out_6), .out_6(alu_10_out_6), .in_4(in_2));
  ALU alu_11 (.out_5(out_5[10]), .B(in_4[10]), .A(in_3[10]), .Cin(alu_10_out_6), .out_6(alu_11_out_6), .in_4(in_2));
  ALU alu_12 (.out_5(out_5[11]), .B(in_4[11]), .A(in_3[11]), .Cin(alu_11_out_6), .out_6(alu_12_out_6), .in_4(in_2));
  ALU alu_13 (.out_5(out_5[12]), .B(in_4[12]), .A(in_3[12]), .Cin(alu_12_out_6), .out_6(alu_13_out_6), .in_4(in_2));
  ALU alu_14 (.out_5(out_5[13]), .B(in_4[13]), .A(in_3[13]), .Cin(alu_13_out_6), .out_6(alu_14_out_6), .in_4(in_2));
  ALU alu_15 (.out_5(out_5[14]), .B(in_4[14]), .A(in_3[14]), .Cin(alu_14_out_6), .out_6(alu_15_out_6), .in_4(in_2));
  ALU alu_16 (.out_5(out_5[15]), .B(in_4[15]), .A(in_3[15]), .Cin(alu_15_out_6), .out_6(Cout), .in_4(in_2));
endmodule

module REG_FIle (
  input  [15:0] WriteData,
  input  [3:0] RS,
  input  [3:0] Write_Reg,
  input  [3:0] RT,
  input  RegWrite,
  input  CLK,
  output [15:0] RD1,
  output [15:0] RD2
);

  wire and_1_out, and_2_out, and_3_out, and_4_out, and_5_out, and_6_out, and_7_out, and_8_out, and_9_out,
       and_10_out, and_11_out, and_12_out, and_13_out, and_14_out, and_15_out, and_16_out, decoder_1_out0,
       decoder_1_out1, decoder_1_out2, decoder_1_out3, decoder_1_out4, decoder_1_out5, decoder_1_out6,
       decoder_1_out7, decoder_1_out8, decoder_1_out9, decoder_1_out10, decoder_1_out11, decoder_1_out12,
       decoder_1_out13, decoder_1_out14, decoder_1_out15;
  wire [15:0] register_1_q, register_2_q, register_3_q, register_4_q, register_5_q, register_6_q,
       register_7_q, register_8_q, register_9_q, register_10_q, register_11_q, register_12_q, register_13_q,
       register_14_q, register_15_q, register_16_q;

  Decoder #(.select(4), .enable("false")) decoder_1 (
    .out0(decoder_1_out0), .out1(decoder_1_out1), .out2(decoder_1_out2), .out3(decoder_1_out3),
    .out4(decoder_1_out4), .out5(decoder_1_out5), .out6(decoder_1_out6), .out7(decoder_1_out7),
    .out8(decoder_1_out8), .out9(decoder_1_out9), .out10(decoder_1_out10), .out11(decoder_1_out11),
    .out12(decoder_1_out12), .out13(decoder_1_out13), .out14(decoder_1_out14), .out15(decoder_1_out15),
    .sel(Write_Reg));
  and and_1 (and_1_out, decoder_1_out0, RegWrite);
  and and_2 (and_2_out, decoder_1_out1, RegWrite);
  and and_3 (and_3_out, decoder_1_out2, RegWrite);
  and and_4 (and_4_out, decoder_1_out3, RegWrite);
  and and_5 (and_5_out, decoder_1_out4, RegWrite);
  and and_6 (and_6_out, decoder_1_out5, RegWrite);
  and and_7 (and_7_out, decoder_1_out6, RegWrite);
  and and_8 (and_8_out, decoder_1_out7, RegWrite);
  and and_9 (and_9_out, decoder_1_out8, RegWrite);
  and and_10 (and_10_out, decoder_1_out9, RegWrite);
  and and_11 (and_11_out, decoder_1_out10, RegWrite);
  and and_12 (and_12_out, decoder_1_out11, RegWrite);
  and and_13 (and_13_out, decoder_1_out12, RegWrite);
  and and_14 (and_14_out, decoder_1_out13, RegWrite);
  and and_15 (and_15_out, decoder_1_out14, RegWrite);
  and and_16 (and_16_out, decoder_1_out15, RegWrite);
  Register #(.width(16)) register_1 (.D(WriteData), .en(and_1_out), .Q(register_1_q), .clk(CLK));  // open: clr
  Register #(.width(16)) register_2 (.D(WriteData), .en(and_2_out), .Q(register_2_q), .clk(CLK));  // open: clr
  Register #(.width(16)) register_3 (.D(WriteData), .en(and_3_out), .Q(register_3_q), .clk(CLK));  // open: clr
  Register #(.width(16)) register_4 (.D(WriteData), .en(and_4_out), .Q(register_4_q), .clk(CLK));  // open: clr
  Register #(.width(16)) register_5 (.D(WriteData), .en(and_5_out), .Q(register_5_q), .clk(CLK));  // open: clr
  Register #(.width(16)) register_6 (.D(WriteData), .en(and_6_out), .Q(register_6_q), .clk(CLK));  // open: clr
  Register #(.width(16)) register_7 (.D(WriteData), .en(and_7_out), .Q(register_7_q), .clk(CLK));  // open: clr
  Register #(.width(16)) register_8 (.D(WriteData), .en(and_8_out), .Q(register_8_q), .clk(CLK));  // open: clr
  Register #(.width(16)) register_9 (.D(WriteData), .en(and_9_out), .Q(register_9_q), .clk(CLK));  // open: clr
  Register #(.width(16)) register_10 (.D(WriteData), .en(and_10_out), .Q(register_10_q), .clk(CLK));  // open: clr
  Register #(.width(16)) register_11 (.D(WriteData), .en(and_11_out), .Q(register_11_q), .clk(CLK));  // open: clr
  Register #(.width(16)) register_12 (.D(WriteData), .en(and_12_out), .Q(register_12_q), .clk(CLK));  // open: clr
  Register #(.width(16)) register_13 (.D(WriteData), .en(and_13_out), .Q(register_13_q), .clk(CLK));  // open: clr
  Register #(.width(16)) register_14 (.D(WriteData), .en(and_14_out), .Q(register_14_q), .clk(CLK));  // open: clr
  Register #(.width(16)) register_15 (.D(WriteData), .en(and_15_out), .Q(register_15_q), .clk(CLK));  // open: clr
  Register #(.width(16)) register_16 (.D(WriteData), .en(and_16_out), .Q(register_16_q), .clk(CLK));  // open: clr
  Multiplexer #(.select(4), .width(16), .enable("false")) multiplexer_1 (
    .in0(register_1_q), .in1(register_2_q), .in2(register_3_q), .in3(register_4_q), .in4(register_5_q),
    .in5(register_6_q), .in6(register_7_q), .in7(register_8_q), .in8(register_9_q), .in9(register_10_q),
    .in10(register_11_q), .in11(register_12_q), .in12(register_13_q), .in13(register_14_q),
    .in14(register_15_q), .in15(register_16_q), .out(RD1), .sel(RS));
  Multiplexer #(.select(4), .width(16), .enable("false")) multiplexer_2 (
    .in0(register_1_q), .in1(register_2_q), .in2(register_3_q), .in3(register_4_q), .in4(register_5_q),
    .in5(register_6_q), .in6(register_7_q), .in7(register_8_q), .in8(register_9_q), .in9(register_10_q),
    .in10(register_11_q), .in11(register_12_q), .in12(register_13_q), .in13(register_14_q),
    .in14(register_15_q), .in15(register_16_q), .out(RD2), .sel(RT));

  // Notes on the sheet:
  //   $zero
  //   $v0
  //   $v1
  //   $a0
  //   $a1
  //   $a2
  //   $t0
  //   $t1
  //   $t2
  //   $t3
  //   $t4
  //   $s0
  //   $s1
  //   $s2
  //   $s3
  //   $s4
endmodule

module _32_Bit_ALU (
  input  [1:0] S,
  input  Cin,
  input  [31:0] A,
  input  [31:0] B,
  output [31:0] Output,
  output Cout
);

  wire n16bit_alu_1_cout;

  _16BIT_ALU u_16bit_alu_1 (
    .in_3(A[15:0]), .in_4(B[15:0]), .out_5(Output[15:0]), .in_1(Cin), .in_2(S), .Cout(n16bit_alu_1_cout));
  _16BIT_ALU u_16bit_alu_2 (
    .in_3(A[31:16]), .in_4(B[31:16]), .out_5(Output[31:16]), .in_1(n16bit_alu_1_cout), .in_2(S), .Cout(Cout));
endmodule

module _32_Bit_REG_File (
  input  [31:0] WriteData,
  input  [3:0] RS,
  input  [3:0] Write_Reg,
  input  [3:0] RT,
  input  RegWrite,
  input  CLK,
  output [31:0] RD1,
  output [31:0] RD2
);

  wire and_1_out, and_2_out, and_3_out, and_4_out, and_5_out, and_6_out, and_7_out, and_8_out, and_9_out,
       and_10_out, and_11_out, and_12_out, and_13_out, and_14_out, and_15_out, and_16_out, decoder_1_out0,
       decoder_1_out1, decoder_1_out2, decoder_1_out3, decoder_1_out4, decoder_1_out5, decoder_1_out6,
       decoder_1_out7, decoder_1_out8, decoder_1_out9, decoder_1_out10, decoder_1_out11, decoder_1_out12,
       decoder_1_out13, decoder_1_out14, decoder_1_out15;
  wire [31:0] register_1_q, register_2_q, register_3_q, register_4_q, register_5_q, register_6_q,
       register_7_q, register_8_q, register_9_q, register_10_q, register_11_q, register_12_q, register_13_q,
       register_14_q, register_15_q, register_16_q;

  Decoder #(.select(4), .enable("false")) decoder_1 (
    .out0(decoder_1_out0), .out1(decoder_1_out1), .out2(decoder_1_out2), .out3(decoder_1_out3),
    .out4(decoder_1_out4), .out5(decoder_1_out5), .out6(decoder_1_out6), .out7(decoder_1_out7),
    .out8(decoder_1_out8), .out9(decoder_1_out9), .out10(decoder_1_out10), .out11(decoder_1_out11),
    .out12(decoder_1_out12), .out13(decoder_1_out13), .out14(decoder_1_out14), .out15(decoder_1_out15),
    .sel(Write_Reg));
  and and_1 (and_1_out, decoder_1_out0, RegWrite);
  and and_2 (and_2_out, decoder_1_out1, RegWrite);
  and and_3 (and_3_out, decoder_1_out2, RegWrite);
  and and_4 (and_4_out, decoder_1_out3, RegWrite);
  and and_5 (and_5_out, decoder_1_out4, RegWrite);
  and and_6 (and_6_out, decoder_1_out5, RegWrite);
  and and_7 (and_7_out, decoder_1_out6, RegWrite);
  and and_8 (and_8_out, decoder_1_out7, RegWrite);
  and and_9 (and_9_out, decoder_1_out8, RegWrite);
  and and_10 (and_10_out, decoder_1_out9, RegWrite);
  and and_11 (and_11_out, decoder_1_out10, RegWrite);
  and and_12 (and_12_out, decoder_1_out11, RegWrite);
  and and_13 (and_13_out, decoder_1_out12, RegWrite);
  and and_14 (and_14_out, decoder_1_out13, RegWrite);
  and and_15 (and_15_out, decoder_1_out14, RegWrite);
  and and_16 (and_16_out, decoder_1_out15, RegWrite);
  Register #(.width(32)) register_1 (.D(WriteData), .en(and_1_out), .Q(register_1_q), .clk(CLK));  // open: clr
  Register #(.width(32)) register_2 (.D(WriteData), .en(and_2_out), .Q(register_2_q), .clk(CLK));  // open: clr
  Register #(.width(32)) register_3 (.D(WriteData), .en(and_3_out), .Q(register_3_q), .clk(CLK));  // open: clr
  Register #(.width(32)) register_4 (.D(WriteData), .en(and_4_out), .Q(register_4_q), .clk(CLK));  // open: clr
  Register #(.width(32)) register_5 (.D(WriteData), .en(and_5_out), .Q(register_5_q), .clk(CLK));  // open: clr
  Register #(.width(32)) register_6 (.D(WriteData), .en(and_6_out), .Q(register_6_q), .clk(CLK));  // open: clr
  Register #(.width(32)) register_7 (.D(WriteData), .en(and_7_out), .Q(register_7_q), .clk(CLK));  // open: clr
  Register #(.width(32)) register_8 (.D(WriteData), .en(and_8_out), .Q(register_8_q), .clk(CLK));  // open: clr
  Register #(.width(32)) register_9 (.D(WriteData), .en(and_9_out), .Q(register_9_q), .clk(CLK));  // open: clr
  Register #(.width(32)) register_10 (.D(WriteData), .en(and_10_out), .Q(register_10_q), .clk(CLK));  // open: clr
  Register #(.width(32)) register_11 (.D(WriteData), .en(and_11_out), .Q(register_11_q), .clk(CLK));  // open: clr
  Register #(.width(32)) register_12 (.D(WriteData), .en(and_12_out), .Q(register_12_q), .clk(CLK));  // open: clr
  Register #(.width(32)) register_13 (.D(WriteData), .en(and_13_out), .Q(register_13_q), .clk(CLK));  // open: clr
  Register #(.width(32)) register_14 (.D(WriteData), .en(and_14_out), .Q(register_14_q), .clk(CLK));  // open: clr
  Register #(.width(32)) register_15 (.D(WriteData), .en(and_15_out), .Q(register_15_q), .clk(CLK));  // open: clr
  Register #(.width(32)) register_16 (.D(WriteData), .en(and_16_out), .Q(register_16_q), .clk(CLK));  // open: clr
  Multiplexer #(.select(4), .width(32), .enable("false")) multiplexer_1 (
    .in0(register_1_q), .in1(register_2_q), .in2(register_3_q), .in3(register_4_q), .in4(register_5_q),
    .in5(register_6_q), .in6(register_7_q), .in7(register_8_q), .in8(register_9_q), .in9(register_10_q),
    .in10(register_11_q), .in11(register_12_q), .in12(register_13_q), .in13(register_14_q),
    .in14(register_15_q), .in15(register_16_q), .out(RD1), .sel(RS));
  Multiplexer #(.select(4), .width(32), .enable("false")) multiplexer_2 (
    .in0(register_1_q), .in1(register_2_q), .in2(register_3_q), .in3(register_4_q), .in4(register_5_q),
    .in5(register_6_q), .in6(register_7_q), .in7(register_8_q), .in8(register_9_q), .in9(register_10_q),
    .in10(register_11_q), .in11(register_12_q), .in12(register_13_q), .in13(register_14_q),
    .in14(register_15_q), .in15(register_16_q), .out(RD2), .sel(RT));

  // Notes on the sheet:
  //   $zero
  //   $v0
  //   $v1
  //   $a0
  //   $a1
  //   $a2
  //   $t0
  //   $t1
  //   $t2
  //   $t3
  //   $t4
  //   $s0
  //   $s1
  //   $s2
  //   $s3
  //   $s4
endmodule

module _32_Bit_DATA_PATH (
  input  in_1,
  input  in_2,
  input  in_3
);

  wire clock_1_out;
  wire [1:0] bit_extender_1_out;
  wire [4:0] instruction_memory_1_rd, instruction_memory_1_rs, instruction_memory_1_rt;
  wire [5:0] instruction_memory_1_fnct;
  wire [31:0] n32_32_bit_reg_1_rd1, n32_32_bit_reg_1_rd2, n32_bit_alu_1_output;

  Instruction_Memory instruction_memory_1 (
    .E(in_1), .in_2(in_2), .CLK(clock_1_out), .Fnct(instruction_memory_1_fnct), .RT(instruction_memory_1_rt),
    .RS(instruction_memory_1_rs), .RD(instruction_memory_1_rd));  // open: Sh_Amt, OP
  Clock clock_1 (.out(clock_1_out));
  _32_32_Bit_REG u_32_32_bit_reg_1 (
    .WriteData(n32_bit_alu_1_output), .Write_Reg(instruction_memory_1_rd), .RegWrite(in_3),
    .CLK(clock_1_out), .RD1(n32_32_bit_reg_1_rd1), .RS(instruction_memory_1_rt), .RD2(n32_32_bit_reg_1_rd2),
    .RT(instruction_memory_1_rs));
  Bit_Extender #(.in_width(6), .out_width(2)) bit_extender_1 (.in(instruction_memory_1_fnct), .out(bit_extender_1_out));
  _32_Bit_ALU u_32_bit_alu_1 (
    .S(bit_extender_1_out), .A(n32_32_bit_reg_1_rd1), .B(n32_32_bit_reg_1_rd2), .Output(n32_bit_alu_1_output));  // open: Cin, Cout
endmodule

module Instruction_Memory (
  input  E,
  input  in_2,
  input  CLK,
  output [5:0] Fnct,
  output [4:0] Sh_Amt,
  output [4:0] RT,
  output [4:0] RS,
  output [4:0] RD,
  output [5:0] OP
);

  wire [1:0] adder_1_out, register_1_q;

  Register #(.width(2)) register_1 (.D(adder_1_out), .en(E), .Q(register_1_q), .clk(CLK), .clr(in_2));
  Adder #(.width(2)) adder_1 (.a(2'b01), .b(register_1_q), .out(adder_1_out));  // open: cin, cout
  ROM #(.addrWidth(2), .dataWidth(32)) rom_1 (.addr(register_1_q), .data({OP, RD, RS, RT, Sh_Amt, Fnct}));  // open: sel

  // Notes on the sheet:
  //   contents of rom_1 (hex, n*v repeats v):
  //   0 51312 15532
endmodule

module _32_32_Bit_REG (
  input  [31:0] WriteData,
  input  [4:0] Write_Reg,
  input  [4:0] RS,
  input  [4:0] RT,
  input  RegWrite,
  input  CLK,
  output [31:0] RD1,
  output [31:0] RD2
);

  wire and_1_out, and_2_out, and_3_out, and_4_out, and_5_out, and_6_out, and_7_out, and_8_out, and_9_out,
       and_10_out, and_11_out, and_12_out, and_13_out, and_14_out, and_15_out, and_16_out, and_17_out,
       and_18_out, and_19_out, and_20_out, and_21_out, and_22_out, and_23_out, and_24_out, and_25_out,
       and_26_out, and_27_out, and_28_out, and_29_out, and_30_out, and_31_out, and_32_out, decoder_1_out0,
       decoder_1_out1, decoder_1_out2, decoder_1_out3, decoder_1_out4, decoder_1_out5, decoder_1_out6,
       decoder_1_out7, decoder_1_out8, decoder_1_out9, decoder_1_out10, decoder_1_out11, decoder_1_out12,
       decoder_1_out13, decoder_1_out14, decoder_1_out15, decoder_1_out16, decoder_1_out17, decoder_1_out18,
       decoder_1_out19, decoder_1_out20, decoder_1_out21, decoder_1_out22, decoder_1_out23, decoder_1_out24,
       decoder_1_out25, decoder_1_out26, decoder_1_out27, decoder_1_out28, decoder_1_out29, decoder_1_out30,
       decoder_1_out31;
  wire [31:0] register_1_q, register_2_q, register_3_q, register_4_q, register_5_q, register_6_q,
       register_7_q, register_8_q, register_9_q, register_10_q, register_11_q, register_12_q, register_13_q,
       register_14_q, register_15_q, register_16_q, register_17_q, register_18_q, register_19_q,
       register_20_q, register_21_q, register_22_q, register_23_q, register_24_q, register_25_q,
       register_26_q, register_27_q, register_28_q, register_29_q, register_30_q, register_31_q,
       register_32_q, undriven;

  Decoder #(.select(5), .enable("false")) decoder_1 (
    .out0(decoder_1_out0), .out1(decoder_1_out1), .out2(decoder_1_out2), .out3(decoder_1_out3),
    .out4(decoder_1_out4), .out5(decoder_1_out5), .out6(decoder_1_out6), .out7(decoder_1_out7),
    .out8(decoder_1_out8), .out9(decoder_1_out9), .out10(decoder_1_out10), .out11(decoder_1_out11),
    .out12(decoder_1_out12), .out13(decoder_1_out13), .out14(decoder_1_out14), .out15(decoder_1_out15),
    .out16(decoder_1_out16), .out17(decoder_1_out17), .out18(decoder_1_out18), .out19(decoder_1_out19),
    .out20(decoder_1_out20), .out21(decoder_1_out21), .out22(decoder_1_out22), .out23(decoder_1_out23),
    .out24(decoder_1_out24), .out25(decoder_1_out25), .out26(decoder_1_out26), .out27(decoder_1_out27),
    .out28(decoder_1_out28), .out29(decoder_1_out29), .out30(decoder_1_out30), .out31(decoder_1_out31),
    .sel(Write_Reg));
  and and_1 (and_1_out, decoder_1_out0, RegWrite);
  and and_2 (and_2_out, decoder_1_out1, RegWrite);
  and and_3 (and_3_out, decoder_1_out2, RegWrite);
  and and_4 (and_4_out, decoder_1_out3, RegWrite);
  and and_5 (and_5_out, decoder_1_out4, RegWrite);
  and and_6 (and_6_out, decoder_1_out5, RegWrite);
  and and_7 (and_7_out, decoder_1_out6, RegWrite);
  and and_8 (and_8_out, decoder_1_out7, RegWrite);
  and and_9 (and_9_out, decoder_1_out8, RegWrite);
  and and_10 (and_10_out, decoder_1_out9, RegWrite);
  and and_11 (and_11_out, decoder_1_out10, RegWrite);
  and and_12 (and_12_out, decoder_1_out11, RegWrite);
  and and_13 (and_13_out, decoder_1_out12, RegWrite);
  and and_14 (and_14_out, decoder_1_out13, RegWrite);
  and and_15 (and_15_out, decoder_1_out14, RegWrite);
  and and_16 (and_16_out, decoder_1_out15, RegWrite);
  and and_17 (and_17_out, decoder_1_out16, RegWrite);
  and and_18 (and_18_out, decoder_1_out17, RegWrite);
  and and_19 (and_19_out, decoder_1_out18, RegWrite);
  and and_20 (and_20_out, decoder_1_out19, RegWrite);
  and and_21 (and_21_out, decoder_1_out20, RegWrite);
  and and_22 (and_22_out, decoder_1_out21, RegWrite);
  and and_23 (and_23_out, decoder_1_out22, RegWrite);
  and and_24 (and_24_out, decoder_1_out23, RegWrite);
  and and_25 (and_25_out, decoder_1_out24, RegWrite);
  and and_26 (and_26_out, decoder_1_out25, RegWrite);
  and and_27 (and_27_out, decoder_1_out26, RegWrite);
  and and_28 (and_28_out, decoder_1_out27, RegWrite);
  and and_29 (and_29_out, decoder_1_out28, RegWrite);
  and and_30 (and_30_out, decoder_1_out29, RegWrite);
  and and_31 (and_31_out, decoder_1_out30, RegWrite);
  and and_32 (and_32_out, decoder_1_out31, RegWrite);
  Register #(.width(32)) register_1 (.D(WriteData), .en(and_1_out), .Q(register_1_q), .clk(CLK));  // open: clr
  Register #(.width(32)) register_2 (.D(WriteData), .en(and_2_out), .Q(register_2_q), .clk(CLK));  // open: clr
  Register #(.width(32)) register_3 (.D(WriteData), .en(and_3_out), .Q(register_3_q), .clk(CLK));  // open: clr
  Register #(.width(32)) register_4 (.D(WriteData), .en(and_4_out), .Q(register_4_q), .clk(CLK));  // open: clr
  Register #(.width(32)) register_5 (.D(WriteData), .en(and_5_out), .Q(register_5_q), .clk(CLK));  // open: clr
  Register #(.width(32)) register_6 (.D(WriteData), .en(and_6_out), .Q(register_6_q), .clk(CLK));  // open: clr
  Register #(.width(32)) register_7 (.D(WriteData), .en(and_7_out), .Q(register_7_q), .clk(CLK));  // open: clr
  Register #(.width(32)) register_8 (.D(WriteData), .en(and_8_out), .Q(register_8_q), .clk(CLK));  // open: clr
  Register #(.width(32)) register_9 (.D(WriteData), .en(and_9_out), .Q(register_9_q), .clk(CLK));  // open: clr
  Register #(.width(32)) register_10 (.D(WriteData), .en(and_10_out), .Q(register_10_q), .clk(CLK));  // open: clr
  Register #(.width(32)) register_11 (.D(WriteData), .en(and_11_out), .Q(register_11_q), .clk(CLK));  // open: clr
  Register #(.width(32)) register_12 (.D(WriteData), .en(and_12_out), .Q(register_12_q), .clk(CLK));  // open: clr
  Register #(.width(32)) register_13 (.D(WriteData), .en(and_13_out), .Q(register_13_q), .clk(CLK));  // open: clr
  Register #(.width(32)) register_14 (.D(WriteData), .en(and_14_out), .Q(register_14_q), .clk(CLK));  // open: clr
  Register #(.width(32)) register_15 (.D(WriteData), .en(and_15_out), .Q(register_15_q), .clk(CLK));  // open: clr
  Register #(.width(32)) register_16 (.D(WriteData), .en(and_16_out), .Q(register_16_q), .clk(CLK));  // open: clr
  Register #(.width(32)) register_17 (.D(undriven), .en(and_17_out), .Q(register_17_q), .clk(CLK));  // open: clr
  Register #(.width(32)) register_18 (.D(undriven), .en(and_18_out), .Q(register_18_q), .clk(CLK));  // open: clr
  Register #(.width(32)) register_19 (.D(undriven), .en(and_19_out), .Q(register_19_q), .clk(CLK));  // open: clr
  Register #(.width(32)) register_20 (.D(undriven), .en(and_20_out), .Q(register_20_q), .clk(CLK));  // open: clr
  Register #(.width(32)) register_21 (.D(undriven), .en(and_21_out), .Q(register_21_q), .clk(CLK));  // open: clr
  Register #(.width(32)) register_22 (.D(undriven), .en(and_22_out), .Q(register_22_q), .clk(CLK));  // open: clr
  Register #(.width(32)) register_23 (.D(undriven), .en(and_23_out), .Q(register_23_q), .clk(CLK));  // open: clr
  Register #(.width(32)) register_24 (.D(undriven), .en(and_24_out), .Q(register_24_q), .clk(CLK));  // open: clr
  Register #(.width(32)) register_25 (.D(undriven), .en(and_25_out), .Q(register_25_q), .clk(CLK));  // open: clr
  Register #(.width(32)) register_26 (.D(undriven), .en(and_26_out), .Q(register_26_q), .clk(CLK));  // open: clr
  Register #(.width(32)) register_27 (.D(undriven), .en(and_27_out), .Q(register_27_q), .clk(CLK));  // open: clr
  Register #(.width(32)) register_28 (.D(undriven), .en(and_28_out), .Q(register_28_q), .clk(CLK));  // open: clr
  Register #(.width(32)) register_29 (.D(undriven), .en(and_29_out), .Q(register_29_q), .clk(CLK));  // open: clr
  Register #(.width(32)) register_30 (.D(undriven), .en(and_30_out), .Q(register_30_q), .clk(CLK));  // open: clr
  Register #(.width(32)) register_31 (.D(undriven), .en(and_31_out), .Q(register_31_q), .clk(CLK));  // open: clr
  Register #(.width(32)) register_32 (.D(undriven), .en(and_32_out), .Q(register_32_q), .clk(CLK));  // open: clr
  Multiplexer #(.select(5), .width(32), .enable("false")) multiplexer_1 (
    .in0(register_1_q), .in1(register_2_q), .in2(register_3_q), .in3(register_4_q), .in4(register_5_q),
    .in5(register_6_q), .in6(register_7_q), .in7(register_8_q), .in8(register_9_q), .in9(register_10_q),
    .in10(register_11_q), .in11(register_12_q), .in12(register_13_q), .in13(register_14_q),
    .in14(register_15_q), .in15(register_16_q), .in16(register_17_q), .in17(register_18_q),
    .in18(register_19_q), .in19(register_20_q), .in20(register_21_q), .in21(register_22_q),
    .in22(register_23_q), .in23(register_24_q), .in24(register_25_q), .in25(register_26_q),
    .in26(register_27_q), .in27(register_28_q), .in28(register_29_q), .in29(register_30_q),
    .in30(register_31_q), .in31(register_32_q), .out(RD1), .sel(RS));
  Multiplexer #(.select(5), .width(32), .enable("false")) multiplexer_2 (
    .in0(register_1_q), .in1(register_2_q), .in2(register_3_q), .in3(register_4_q), .in4(register_5_q),
    .in5(register_6_q), .in6(register_7_q), .in7(register_8_q), .in8(register_9_q), .in9(register_10_q),
    .in10(register_11_q), .in11(register_12_q), .in12(register_13_q), .in13(register_14_q),
    .in14(register_15_q), .in15(register_16_q), .in16(register_17_q), .in17(register_18_q),
    .in18(register_19_q), .in19(register_20_q), .in20(register_21_q), .in21(register_22_q),
    .in22(register_23_q), .in23(register_24_q), .in24(register_25_q), .in25(register_26_q),
    .in26(register_27_q), .in27(register_28_q), .in28(register_29_q), .in29(register_30_q),
    .in30(register_31_q), .in31(register_32_q), .out(RD2), .sel(RT));

  // Notes on the sheet:
  //   $zero
  //   $zero
  //   $v0
  //   $v1
  //   $a0
  //   $a1
  //   $a2
  //   $t0
  //   $t1
  //   $t2
  //   $t3
  //   $t4
  //   $s0
  //   $s1
  //   $s2
  //   $s3
  //   $s4
  //   $v0
  //   $v1
  //   $a0
  //   $a1
  //   $a2
  //   $t0
  //   $t1
  //   $t2
  //   $t3
  //   $t4
  //   $s0
  //   $s1
  //   $s2
  //   $s3
  //   $s4
endmodule
