// Logisim project Seven_Segment.circ as structural Verilog: 6 circuits, main circuit main
module main (
  input  A,
  input  B,
  input  C
);

  wire n7_segment_display_project_1_a_2, n7_segment_display_project_1_b_2, n7_segment_display_project_1_c_2,
       n7_segment_display_project_1_d, n7_segment_display_project_1_e, n7_segment_display_project_1_f,
       n7_segment_display_project_1_g, using_nand_gates_1_a_2, using_nand_gates_1_b_2,
       using_nand_gates_1_c_2, using_nand_gates_1_d, using_nand_gates_1_e, using_nand_gates_1_f,
       using_nand_gates_1_g, using_nor_gates_1_a_2, using_nor_gates_1_b_2, using_nor_gates_1_c_2,
       using_nor_gates_1_d, using_nor_gates_1_e, using_nor_gates_1_f, using_nor_gates_1_g, using_pos_1_a_2,
       using_pos_1_b_2, using_pos_1_c_2, using_pos_1_d, using_pos_1_e, using_pos_1_f, using_pos_1_g,
       using_sop_1_a_2, using_sop_1_b_2, using_sop_1_c_2, using_sop_1_d, using_sop_1_e, using_sop_1_f,
       using_sop_1_g;

  _7_Segment_Display_Project u_7_segment_display_project_1 (
    .A(A), .B(B), .C(C), .a_2(n7_segment_display_project_1_a_2), .b_2(n7_segment_display_project_1_b_2),
    .c_2(n7_segment_display_project_1_c_2), .d(n7_segment_display_project_1_d),
    .e(n7_segment_display_project_1_e), .f(n7_segment_display_project_1_f), .g(n7_segment_display_project_1_g));
  using_NAND_gates using_nand_gates_1 (
    .a_2(using_nand_gates_1_a_2), .b_2(using_nand_gates_1_b_2), .c_2(using_nand_gates_1_c_2),
    .d(using_nand_gates_1_d), .e(using_nand_gates_1_e), .f(using_nand_gates_1_f), .g(using_nand_gates_1_g),
    .A(A), .B(B), .C(C));
  using_NOR_gates using_nor_gates_1 (
    .a_2(using_nor_gates_1_a_2), .b_2(using_nor_gates_1_b_2), .c_2(using_nor_gates_1_c_2),
    .d(using_nor_gates_1_d), .e(using_nor_gates_1_e), .f(using_nor_gates_1_f), .g(using_nor_gates_1_g),
    .A(A), .B(B), .C(C));
  using_SOP using_sop_1 (
    .a_2(using_sop_1_a_2), .b_2(using_sop_1_b_2), .c_2(using_sop_1_c_2), .d(using_sop_1_d),
    .e(using_sop_1_e), .f(using_sop_1_f), .g(using_sop_1_g), .A(A), .B(B), .C(C));
  using_POS using_pos_1 (
    .a_2(using_pos_1_a_2), .b_2(using_pos_1_b_2), .c_2(using_pos_1_c_2), .d(using_pos_1_d),
    .e(using_pos_1_e), .f(using_pos_1_f), .g(using_pos_1_g), .A(A), .B(B), .C(C));
  _7_Segment_Display u_7_segment_display_1 (
    .g(n7_segment_display_project_1_g), .f(n7_segment_display_project_1_f),
    .a(n7_segment_display_project_1_a_2), .b(n7_segment_display_project_1_b_2),
    .e(n7_segment_display_project_1_e), .d(n7_segment_display_project_1_d),
    .c(n7_segment_display_project_1_c_2));  // open: dp
  _7_Segment_Display u_7_segment_display_2 (
    .g(using_nand_gates_1_g), .f(using_nand_gates_1_f), .a(using_nand_gates_1_a_2),
    .b(using_nand_gates_1_b_2), .e(using_nand_gates_1_e), .d(using_nand_gates_1_d), .c(using_nand_gates_1_c_2));  // open: dp
  _7_Segment_Display u_7_segment_display_3 (
    .g(using_nor_gates_1_g), .f(using_nor_gates_1_f), .a(using_nor_gates_1_a_2), .b(using_nor_gates_1_b_2),
    .e(using_nor_gates_1_e), .d(using_nor_gates_1_d), .c(using_nor_gates_1_c_2));  // open: dp
  _7_Segment_Display u_7_segment_display_4 (
    .g(using_sop_1_g), .f(using_sop_1_f), .a(using_sop_1_a_2), .b(using_sop_1_b_2), .e(using_sop_1_e),
    .d(using_sop_1_d), .c(using_sop_1_c_2));  // open: dp
  _7_Segment_Display u_7_segment_display_5 (
    .g(using_pos_1_g), .f(using_pos_1_f), .a(using_pos_1_a_2), .b(using_pos_1_b_2), .e(using_pos_1_e),
    .d(using_pos_1_d), .c(using_pos_1_c_2));  // open: dp

  // Notes on the sheet:
  //   A     B     C
  //   0     0     0
  //   5
  //   7
  //   0     0     1
  //   Z
  //   0     1     0
  //   0     1     1
  //   e
  //   n
  //   1     0     0
  //   1     0     1
  //   2
  //   6
  //   1     1     0
  //   Represents
endmodule

module _7_Segment_Display_Project (
  input  A,
  input  B,
  input  C,
  output a_2,
  output b_2,
  output c_2,
  output d,
  output e,
  output f,
  output g
);

  wire and_1_out, and_2_out, and_3_out, and_4_out, and_5_out, and_6_out, and_7_out, and_8_out, and_9_out,
       and_10_out, and_11_out, and_12_out, and_13_out, not_1_out, not_2_out, not_3_out, not_4_out, not_5_out,
       not_6_out, not_7_out, not_8_out, not_9_out, not_10_out, not_11_out, not_12_out, not_13_out,
       not_14_out, not_15_out, not_16_out, or_3_out, or_5_out;

  not not_1 (not_1_out, A);
  not not_2 (not_2_out, B);
  not not_3 (not_3_out, B);
  not not_4 (not_4_out, A);
  not not_5 (not_5_out, A);
  not not_6 (not_6_out, B);
  not not_7 (not_7_out, C);
  not not_8 (not_8_out, A);
  not not_9 (not_9_out, C);
  not not_10 (not_10_out, A);
  not not_11 (not_11_out, B);
  not not_12 (not_12_out, C);
  and and_1 (and_1_out, not_1_out, not_2_out);
  and and_2 (and_2_out, not_3_out, C);
  not not_13 (not_13_out, C);
  not not_14 (not_14_out, B);
  and and_3 (and_3_out, not_4_out, B);
  not not_15 (not_15_out, C);
  and and_4 (and_4_out, not_5_out, not_6_out);
  and and_5 (and_5_out, A, not_7_out);
  and and_6 (and_6_out, not_8_out, not_9_out);
  or or_1 (e, B, A);
  and and_7 (and_7_out, not_10_out, not_11_out);
  not not_16 (not_16_out, C);
  or or_2 (g, not_12_out, A);
  or or_3 (or_3_out, and_1_out, and_2_out);
  and and_8 (and_8_out, B, not_13_out);
  and and_9 (and_9_out, not_14_out, C);
  and and_10 (and_10_out, and_3_out, not_15_out);
  or or_4 (c_2, and_4_out, and_5_out);
  or or_5 (or_5_out, and_6_out, B);
  and and_11 (and_11_out, A, C);
  and and_12 (and_12_out, and_7_out, not_16_out);
  and and_13 (and_13_out, A, B);
  or or_6 (a_2, or_3_out, and_8_out);
  or or_7 (b_2, and_9_out, and_10_out);
  or or_8 (d, or_5_out, and_11_out);
  or or_9 (f, and_12_out, and_13_out);

  // Notes on the sheet:
  //   e = A+B
  //   g = A+C'
  //   a = A'B'+B'C+BC'
  //   b = B'C+A'BC'
  //   c = A'B'+AC'
  //   d = A'C'+B+AC
  //   f = A'B'C'+AB
  //   This is the most Optimized circuit using K-Map.As K-Map gives the simplest Boolean expression without physically performing any boolean algebra.
  //   A     B     C
  //   0     0     0
  //   0     0     1
  //   0     1     0
  //   0     1     1
  //   1     0     0
  //   1     0     1
  //   1     1     0
  //   Represents
  //   5
  //   7
  //   Z
  //   e
  //   n
  //   2
  //   6
endmodule

module using_NAND_gates (
  input  A,
  input  B,
  input  C,
  output a_2,
  output b_2,
  output c_2,
  output d,
  output e,
  output f,
  output g
);

  wire nand_1_out, nand_2_out, nand_3_out, nand_4_out, nand_5_out, nand_6_out, nand_7_out, nand_8_out,
       nand_9_out, nand_10_out, nand_11_out, nand_12_out, nand_13_out, nand_14_out, nand_15_out, nand_16_out,
       nand_17_out, nand_18_out, nand_19_out, nand_20_out, nand_21_out, nand_22_out, nand_23_out,
       nand_25_out, nand_26_out, nand_27_out, nand_29_out, nand_30_out, nand_31_out, nand_32_out,
       nand_33_out, nand_35_out, nand_36_out, nand_37_out, nand_38_out, nand_39_out, nand_40_out, nand_41_out;

  nand nand_1 (nand_1_out, A, A);
  nand nand_2 (nand_2_out, B, B);
  nand nand_3 (nand_3_out, B, B);
  nand nand_4 (nand_4_out, A, A);
  nand nand_5 (nand_5_out, A, A);
  nand nand_6 (nand_6_out, B, B);
  nand nand_7 (nand_7_out, C, C);
  nand nand_8 (nand_8_out, A, A);
  nand nand_9 (nand_9_out, C, C);
  nand nand_10 (nand_10_out, B, B);
  nand nand_11 (nand_11_out, A, A);
  nand nand_12 (nand_12_out, A, A);
  nand nand_13 (nand_13_out, B, B);
  nand nand_14 (nand_14_out, A, A);
  nand nand_15 (nand_15_out, nand_1_out, nand_2_out);
  nand nand_16 (nand_16_out, nand_3_out, C);
  nand nand_17 (nand_17_out, C, C);
  nand nand_18 (nand_18_out, nand_4_out, B);
  nand nand_19 (nand_19_out, nand_5_out, nand_6_out);
  nand nand_20 (nand_20_out, A, nand_7_out);
  nand nand_21 (nand_21_out, nand_8_out, nand_9_out);
  nand nand_22 (nand_22_out, B, B);
  nand nand_23 (nand_23_out, A, C);
  nand nand_24 (e, nand_10_out, nand_11_out);
  nand nand_25 (nand_25_out, nand_12_out, nand_13_out);
  nand nand_26 (nand_26_out, C, C);
  nand nand_27 (nand_27_out, A, B);
  nand nand_28 (g, C, nand_14_out);
  nand nand_29 (nand_29_out, nand_15_out, nand_16_out);
  nand nand_30 (nand_30_out, B, nand_17_out);
  nand nand_31 (nand_31_out, B, B);
  nand nand_32 (nand_32_out, nand_18_out, nand_18_out);
  nand nand_33 (nand_33_out, C, C);
  nand nand_34 (c_2, nand_19_out, nand_20_out);
  nand nand_35 (nand_35_out, nand_21_out, nand_22_out);
  nand nand_36 (nand_36_out, nand_25_out, nand_25_out);
  nand nand_37 (nand_37_out, nand_29_out, nand_29_out);
  nand nand_38 (nand_38_out, nand_31_out, C);
  nand nand_39 (nand_39_out, nand_32_out, nand_33_out);
  nand nand_40 (nand_40_out, nand_35_out, nand_35_out);
  nand nand_41 (nand_41_out, nand_36_out, nand_26_out);
  nand nand_42 (a_2, nand_37_out, nand_30_out);
  nand nand_43 (b_2, nand_38_out, nand_39_out);
  nand nand_44 (d, nand_40_out, nand_23_out);
  nand nand_45 (f, nand_41_out, nand_27_out);
endmodule

module using_NOR_gates (
  input  A,
  input  B,
  input  C,
  output a_2,
  output b_2,
  output c_2,
  output d,
  output e,
  output f,
  output g
);

  wire nor_1_out, nor_2_out, nor_3_out, nor_4_out, nor_5_out, nor_6_out, nor_7_out, nor_8_out, nor_9_out,
       nor_10_out, nor_11_out, nor_12_out, nor_13_out, nor_14_out, nor_15_out, nor_16_out, nor_17_out,
       nor_18_out, nor_19_out, nor_20_out, nor_21_out, nor_22_out, nor_23_out, nor_24_out, nor_25_out,
       nor_26_out, nor_27_out, nor_28_out, nor_29_out, nor_30_out, nor_32_out, nor_34_out, nor_35_out,
       nor_37_out, nor_38_out, nor_40_out;

  nor nor_1 (nor_1_out, C, C);
  nor nor_2 (nor_2_out, B, B);
  nor nor_3 (nor_3_out, C, C);
  nor nor_4 (nor_4_out, B, B);
  nor nor_5 (nor_5_out, A, A);
  nor nor_6 (nor_6_out, A, C);
  nor nor_7 (nor_7_out, A, A);
  nor nor_8 (nor_8_out, C, C);
  nor nor_9 (nor_9_out, A, B);
  nor nor_10 (nor_10_out, A, A);
  nor nor_11 (nor_11_out, B, B);
  nor nor_12 (nor_12_out, C, C);
  nor nor_13 (nor_13_out, A, B);
  nor nor_14 (nor_14_out, B, nor_1_out);
  nor nor_15 (nor_15_out, nor_2_out, C);
  nor nor_16 (nor_16_out, B, nor_3_out);
  nor nor_17 (nor_17_out, C, nor_4_out);
  nor nor_18 (nor_18_out, A, B);
  nor nor_19 (nor_19_out, nor_5_out, C);
  nor nor_20 (nor_20_out, nor_7_out, nor_8_out);
  nor nor_21 (nor_21_out, A, B);
  nor nor_22 (nor_22_out, nor_9_out, nor_9_out);
  nor nor_23 (nor_23_out, nor_22_out, C);
  nor nor_24 (nor_24_out, nor_10_out, nor_11_out);
  nor nor_25 (nor_25_out, A, nor_12_out);
  nor nor_26 (nor_26_out, nor_13_out, nor_14_out);
  nor nor_27 (nor_27_out, A, nor_28_out);
  nor nor_28 (nor_28_out, nor_17_out, nor_17_out);
  nor nor_29 (nor_29_out, nor_18_out, nor_19_out);
  nor nor_30 (nor_30_out, nor_6_out, B);
  nor nor_31 (e, nor_21_out, nor_21_out);
  nor nor_32 (nor_32_out, nor_23_out, nor_24_out);
  nor nor_33 (g, nor_25_out, nor_25_out);
  nor nor_34 (nor_34_out, nor_26_out, nor_26_out);
  nor nor_35 (nor_35_out, nor_16_out, nor_27_out);
  nor nor_36 (c_2, nor_29_out, nor_29_out);
  nor nor_37 (nor_37_out, nor_30_out, nor_30_out);
  nor nor_38 (nor_38_out, nor_37_out, nor_20_out);
  nor nor_39 (f, nor_32_out, nor_32_out);
  nor nor_40 (nor_40_out, nor_34_out, nor_15_out);
  nor nor_41 (b_2, nor_35_out, nor_35_out);
  nor nor_42 (d, nor_38_out, nor_38_out);
  nor nor_43 (a_2, nor_40_out, nor_40_out);
endmodule

module using_SOP (
  input  A,
  input  B,
  input  C,
  output a_2,
  output b_2,
  output c_2,
  output d,
  output e,
  output f,
  output g
);

  wire and_1_out, and_2_out, and_3_out, and_4_out, and_5_out, and_6_out, and_7_out, and_8_out, and_9_out,
       and_10_out, and_11_out, and_12_out, and_13_out, and_14_out, and_15_out, and_16_out, and_17_out,
       and_18_out, and_19_out, and_20_out, and_21_out, and_22_out, and_23_out, and_24_out, and_25_out,
       and_26_out, not_1_out, not_2_out, not_3_out, or_1_out, or_4_out, or_5_out, or_6_out, or_8_out;

  not not_1 (not_1_out, A);
  not not_2 (not_2_out, B);
  not not_3 (not_3_out, C);
  and and_1 (and_1_out, not_1_out, not_2_out);
  and and_2 (and_2_out, not_2_out, C);
  and and_3 (and_3_out, B, not_3_out);
  and and_4 (and_4_out, not_2_out, C);
  and and_5 (and_5_out, not_1_out, B);
  and and_6 (and_6_out, and_5_out, not_3_out);
  and and_7 (and_7_out, not_1_out, not_2_out);
  and and_8 (and_8_out, A, not_3_out);
  and and_9 (and_9_out, not_1_out, not_3_out);
  and and_10 (and_10_out, not_1_out, B);
  and and_11 (and_11_out, and_10_out, C);
  and and_12 (and_12_out, A, not_2_out);
  and and_13 (and_13_out, and_12_out, C);
  and and_14 (and_14_out, A, B);
  and and_15 (and_15_out, and_14_out, not_3_out);
  and and_16 (and_16_out, not_1_out, B);
  and and_17 (and_17_out, A, not_2_out);
  and and_18 (and_18_out, A, B);
  and and_19 (and_19_out, and_18_out, not_3_out);
  and and_20 (and_20_out, not_1_out, not_2_out);
  and and_21 (and_21_out, and_20_out, not_3_out);
  and and_22 (and_22_out, A, B);
  and and_23 (and_23_out, and_22_out, not_3_out);
  and and_24 (and_24_out, not_1_out, not_3_out);
  and and_25 (and_25_out, A, not_2_out);
  and and_26 (and_26_out, A, not_3_out);
  or or_1 (or_1_out, and_1_out, and_2_out);
  or or_2 (b_2, and_4_out, and_6_out);
  or or_3 (c_2, and_7_out, and_8_out);
  or or_4 (or_4_out, and_9_out, and_11_out);
  or or_5 (or_5_out, and_13_out, and_15_out);
  or or_6 (or_6_out, and_16_out, and_17_out);
  or or_7 (f, and_21_out, and_23_out);
  or or_8 (or_8_out, and_24_out, and_25_out);
  or or_9 (a_2, or_1_out, and_3_out);
  or or_10 (d, or_4_out, or_5_out);
  or or_11 (e, or_6_out, and_19_out);
  or or_12 (g, or_8_out, and_26_out);
endmodule

module using_POS (
  input  A,
  input  B,
  input  C,
  output a_2,
  output b_2,
  output c_2,
  output d,
  output e,
  output f,
  output g
);

  wire and_2_out, and_6_out, not_1_out, not_2_out, not_3_out, or_1_out, or_2_out, or_3_out, or_4_out,
       or_5_out, or_6_out, or_7_out, or_8_out, or_9_out, or_10_out, or_11_out, or_12_out, or_13_out,
       or_14_out, or_15_out, or_16_out, or_17_out, or_18_out, or_19_out, or_20_out, or_21_out, or_22_out,
       or_23_out, or_24_out;

  not not_1 (not_1_out, A);
  not not_2 (not_2_out, B);
  not not_3 (not_3_out, C);
  or or_1 (or_1_out, A, not_2_out);
  or or_2 (or_2_out, or_1_out, not_3_out);
  or or_3 (or_3_out, not_1_out, B);
  or or_4 (or_4_out, or_3_out, C);
  or or_5 (or_5_out, B, C);
  or or_6 (or_6_out, A, not_2_out);
  or or_7 (or_7_out, or_6_out, not_3_out);
  or or_8 (or_8_out, not_1_out, not_2_out);
  or or_9 (or_9_out, or_8_out, C);
  or or_10 (or_10_out, A, not_2_out);
  or or_11 (or_11_out, not_1_out, B);
  or or_12 (or_12_out, or_11_out, not_3_out);
  or or_13 (or_13_out, A, B);
  or or_14 (or_14_out, or_13_out, not_3_out);
  or or_15 (or_15_out, not_1_out, B);
  or or_16 (or_16_out, or_15_out, C);
  or or_17 (or_17_out, A, B);
  or or_18 (or_18_out, or_17_out, C);
  or or_19 (or_19_out, A, B);
  or or_20 (or_20_out, or_19_out, not_3_out);
  or or_21 (or_21_out, B, not_3_out);
  or or_22 (or_22_out, A, not_2_out);
  or or_23 (or_23_out, not_1_out, B);
  or or_24 (or_24_out, or_23_out, C);
  or or_25 (g, A, not_3_out);
  and and_1 (a_2, or_2_out, or_4_out);
  and and_2 (and_2_out, or_5_out, or_7_out);
  and and_3 (c_2, or_10_out, or_12_out);
  and and_4 (d, or_14_out, or_16_out);
  and and_5 (e, or_18_out, or_20_out);
  and and_6 (and_6_out, or_21_out, or_22_out);
  and and_7 (b_2, and_2_out, or_9_out);
  and and_8 (f, and_6_out, or_24_out);
endmodule
